// Logisim project control.circ as structural Verilog: 1 circuit, main circuit main
module main (
  input  start,
  input  is_counter_32,
  input  is_0bit_1,
  input  clock,
  output upper_reg_en,
  output shift_right_mux,
  output select_shifted_val,
  output lower_reg_en,
  output sum_with_0,
  output counter_flag,
  output counter_en,
  output [2:0] state
);

  wire and_1_out, and_2_out, and_3_out, and_4_out, and_5_out, and_6_out, and_7_out, and_8_out, and_9_out,
       and_10_out, and_11_out, and_13_out, not_1_out, not_2_out, not_3_out, not_4_out, not_5_out, not_6_out,
       not_7_out, not_8_out, not_9_out;
  wire [2:0] or_3_out;

  Register #(.width(3)) register_1 (.D(or_3_out), .en(1'b1), .Q(state), .clk(clock));  // open: clr
  not not_1 (not_1_out, state[2]);
  not not_2 (not_2_out, state[1]);
  not not_3 (not_3_out, state[0]);
  not not_4 (not_4_out, start);
  not not_5 (not_5_out, is_counter_32);
  not not_6 (not_6_out, is_0bit_1);
  and and_1 (and_1_out, not_1_out, state[1], not_3_out, not_5_out, not_6_out);
  and and_2 (and_2_out, not_1_out, state[1], state[0]);
  and and_3 (and_3_out, state[2], not_2_out, not_3_out);
  and and_4 (and_4_out, not_1_out, not_2_out, state[0]);
  and and_5 (and_5_out, not_1_out, state[1], not_3_out, not_5_out, is_0bit_1);
  and and_6 (and_6_out, state[2], not_2_out, state[0]);
  and and_7 (and_7_out, not_1_out, not_2_out, not_3_out, start);
  and and_8 (and_8_out, not_1_out, state[1], not_3_out, not_5_out, is_0bit_1);
  and and_9 (and_9_out, not_1_out, state[1], state[0]);
  and and_10 (and_10_out, state[2], not_2_out, not_3_out);
  or or_1 (or_3_out[2], and_1_out, and_2_out, and_3_out);
  or or_2 (or_3_out[1], and_4_out, and_5_out, and_6_out);
  or or_3 (or_3_out[0], and_7_out, and_8_out, and_9_out, and_10_out);
  not not_7 (not_7_out, or_3_out[2]);
  not not_8 (not_8_out, or_3_out[1]);
  not not_9 (not_9_out, or_3_out[0]);
  and and_11 (and_11_out, not_7_out, or_3_out[1], or_3_out[0]);
  and and_12 (sum_with_0, or_3_out[2], not_8_out, not_9_out);
  and and_13 (and_13_out, not_7_out, not_8_out, or_3_out[0]);
  and and_14 (counter_en, or_3_out[0], not_8_out, or_3_out[2]);
  or or_4 (select_shifted_val, and_11_out, sum_with_0);
  or or_5 (lower_reg_en, sum_with_0, and_11_out, and_13_out);

  assign counter_flag = counter_en;
  assign shift_right_mux = select_shifted_val;
  assign upper_reg_en = select_shifted_val;
endmodule
