// Logisim project datapath.circ as structural Verilog: 1 circuit, main circuit main
module main (
  input  [31:0] mult,
  input  [31:0] lower,
  input  select_shifted_val,
  input  counter_en,
  input  upper_reg_en,
  input  lower_reg_en,
  input  sum_with_0,
  input  shift_right_mux,
  input  counter_flag,
  input  clock,
  output is_counter_32,
  output [31:0] HI,
  output [31:0] LO,
  output is_0bit_1
);

  wire [0:0] adder_1_out_2;
  wire [31:0] adder_1_out, counter_q, multiplexer_1_out, multiplexer_2_out, multiplexer_3_out,
       multiplexer_4_out, multiplexer_5_out;

  Multiplexer #(.width(32)) multiplexer_1 (
    .in0(lower), .in1(multiplexer_3_out), .out(multiplexer_1_out), .sel(shift_right_mux));  // open: en
  Register #(.width(32)) register_1 (.D(adder_1_out), .en(upper_reg_en), .Q(HI), .clk(clock));  // open: clr
  Register #(.width(32)) register_2 (.D(multiplexer_1_out), .en(lower_reg_en), .Q(LO), .clk(clock));  // open: clr
  Multiplexer #(.width(32)) multiplexer_2 (
    .in0(mult), .in1({32{1'b0}}), .out(multiplexer_2_out), .sel(sum_with_0));  // open: en
  Multiplexer #(.width(32)) multiplexer_3 (
    .in0(LO), .in1({adder_1_out_2[0], LO[31:1]}), .out(multiplexer_3_out), .sel(select_shifted_val));  // open: en
  Register #(.width(32)) counter (
    .D({adder_1_out[30:0], adder_1_out_2[0]}), .en(counter_en), .Q(counter_q), .clk(clock));  // open: clr
  Multiplexer #(.width(32)) multiplexer_4 (
    .in0(multiplexer_2_out), .in1(counter_q), .out(multiplexer_4_out), .sel(counter_flag));  // open: en
  Multiplexer #(.width(32)) multiplexer_5 (
    .in0(HI), .in1(32'h1), .out(multiplexer_5_out), .sel(counter_flag));  // open: en
  Comparator #(.width(32)) comparator_1 (.a(counter_q), .b(32'h20), .eq(is_counter_32));  // open: gt, lt
  Adder #(.width(32)) adder_1 (
    .a(multiplexer_4_out), .b(multiplexer_5_out), .out({adder_1_out[30:0], adder_1_out_2[0]}),
    .cout(adder_1_out[31]));  // open: cin
  Comparator #(.width(1)) comparator_2 (.a(LO[0]), .b(1'b1), .eq(is_0bit_1));  // open: gt, lt
endmodule
