// Logisim project mult32.circ as structural Verilog: 1 circuit, main circuit main
module main (
  input  [31:0] multipicant,
  input  [31:0] multiplier,
  output [2:0] state,
  output [31:0] HI32Bit,
  output [31:0] LO32bit
);

  wire button_1_out, clock_1_out, main_1_is_0bit_1, main_1_is_counter_32, main_2_counter_en,
       main_2_counter_flag, main_2_lower_reg_en, main_2_select_shifted_val, main_2_shift_right_mux,
       main_2_sum_with_0, main_2_upper_reg_en;

  Clock clock_1 (.out(clock_1_out));
  Button button_1 (.out(button_1_out));
  datapath_main main_1 (
    .lower(multipicant), .select_shifted_val(main_2_select_shifted_val), .counter_en(main_2_counter_en),
    .upper_reg_en(main_2_upper_reg_en), .lower_reg_en(main_2_lower_reg_en), .sum_with_0(main_2_sum_with_0),
    .shift_right_mux(main_2_shift_right_mux), .counter_flag(main_2_counter_flag), .clock(clock_1_out),
    .mult(multiplier), .is_counter_32(main_1_is_counter_32), .HI(HI32Bit), .LO(LO32bit),
    .is_0bit_1(main_1_is_0bit_1));
  control_main main_2 (
    .start(button_1_out), .is_counter_32(main_1_is_counter_32), .is_0bit_1(main_1_is_0bit_1),
    .clock(clock_1_out), .upper_reg_en(main_2_upper_reg_en), .shift_right_mux(main_2_shift_right_mux),
    .select_shifted_val(main_2_select_shifted_val), .lower_reg_en(main_2_lower_reg_en),
    .sum_with_0(main_2_sum_with_0), .counter_flag(main_2_counter_flag), .counter_en(main_2_counter_en),
    .state(state));
endmodule
